# Fritzing sketch Electronica (saved by Fritzing 0.9.3b)

parts:
  Componente1 = Arduino Uno (Rev3)
  J1 = Basic Servo
  J2 = Basic Servo
  J3 = Basic Servo
  J4 = Basic Servo

nets:
  GND: Componente1.GND, J1.gnd, J2.gnd, J3.gnd, J4.gnd
  N1: Componente1.D2, J1.pulse
  N2: Componente1.D3_PWM, J2.pulse
  N3: Componente1.D4, J3.pulse
  N4: Componente1.D5_PWM, J4.pulse
  VCC: Componente1.5V, J1.vcc, J2.vcc, J3.vcc, J4.vcc

notes:
  Guia
  Dispnsador Bottella
